// Logisim project CPU.circ as structural Verilog: 3 circuits, main circuit main
module main (
  input  Reset,
  input  Start
);

  wire and_1_out, and_2_out, and_3_out, and_4_out, and_5_out, and_6_out, and_7_out, and_8_out, and_9_out,
       and_10_out, and_11_out, and_12_out, and_13_out, and_14_out, and_15_out, and_16_out, and_17_out,
       and_18_out, and_19_out, and_20_out, and_21_out, and_22_out, and_23_out, and_24_out, and_25_out,
       and_26_out, and_27_out, and_28_out, and_29_out, and_30_out, and_31_out, and_33_out, and_34_out,
       and_35_out, and_36_out, and_37_out, and_39_out, and_40_out, and_50_out, and_51_out, clock_1_out,
       comparator_1_eq, comparator_1_gt, comparator_1_lt, decoder_1_out0, decoder_1_out1, decoder_2_out0,
       decoder_2_out1, decoder_2_out2, decoder_2_out3, decoder_2_out4, decoder_3_out0, decoder_3_out1,
       decoder_3_out2, decoder_3_out3, decoder_4_out0, decoder_4_out1, decoder_4_out2, decoder_4_out3,
       decoder_4_out4, decoder_5_out1, decoder_5_out2, decoder_5_out3, decoder_5_out4, decoder_5_out5,
       decoder_5_out6, decoder_5_out7, decoder_5_out8, decoder_5_out9, decoder_5_out10, decoder_5_out11,
       decoder_5_out13, decoder_5_out14, decoder_5_out15, demultiplexer_1_out0, demultiplexer_1_out1,
       keyboard_1_avail, multiplexer_1_out, not_1_out, not_2_out, not_3_out, not_4_out, not_5_out, not_6_out,
       not_7_out, not_8_out, not_9_out, or_1_out, or_2_out, or_3_out, or_4_out, or_5_out, or_6_out, or_7_out,
       or_8_out, or_9_out, or_10_out, or_11_out, or_12_out, register_12_q, undriven;
  wire [1:0] register_9_q_3;
  wire [3:0] controlled_buffer_1_out_2, counter_1_q, register_3_q, register_4_q, register_5_q, register_11_q;
  wire [3:2] register_9_q;
  wire [6:0] keyboard_1_data;
  wire [7:0] alu_8bit_1_c0, controlled_buffer_3_out, controlled_buffer_9_out, ram_1_data, register_1_out,
       register_2_out, register_6_q, register_7_q, register_8_q, register_10_q, rom_1_data, rom_2_data;
  wire [7:4] controlled_buffer_1_out, register_9_q_2;

  Clock clock_1 (.out(clock_1_out));
  and and_1 (and_1_out, clock_1_out, Start, not_1_out);
  not not_1 (not_1_out, or_11_out);
  not not_2 (not_2_out, decoder_5_out13);
  and and_2 (and_2_out, decoder_1_out0, not_2_out, and_1_out);
  and and_3 (and_3_out, decoder_1_out1, not_2_out, and_1_out);
  and and_4 (and_4_out, and_1_out, and_30_out);
  Demultiplexer #(.select(4)) demultiplexer_1 (
    .out0(demultiplexer_1_out0), .out1(demultiplexer_1_out1), .in(and_4_out),
    .sel({register_9_q, register_9_q_3}));  // open: out2, out3, out4, out5, out6, out7, out8, out9, out10, out11, out12, out13, out14, out15, en
  Register register_1 (
    .In(controlled_buffer_3_out), .S(demultiplexer_1_out0), .C(and_2_out), .R(Reset), .Out(register_1_out));
  Register register_2 (
    .In(controlled_buffer_3_out), .S(demultiplexer_1_out1), .C(and_3_out), .R(Reset), .Out(register_2_out));
  and and_5 (and_5_out, and_1_out, and_51_out);
  Register_part #(.width(4)) register_3 (
    .D(controlled_buffer_3_out[3:0]), .Q(register_3_q), .clk(and_5_out), .clr(Reset));  // open: en
  ROM rom_1 (.addr(register_1_out), .data(rom_1_data));  // open: sel
  ROM rom_2 (.addr(register_2_out), .data(rom_2_data));  // open: sel
  Decoder #(.select(4)) decoder_1 (
    .out0(decoder_1_out0), .out1(decoder_1_out1), .sel(register_3_q));  // open: out2, out3, out4, out5, out6, out7, out8, out9, out10, out11, out12, out13, out14, out15, en
  assign {controlled_buffer_1_out, controlled_buffer_1_out_2} = decoder_1_out0 ? rom_1_data : 8'bz;  // Controlled_Buffer controlled_buffer_1
  assign {controlled_buffer_1_out, controlled_buffer_1_out_2} = decoder_1_out1 ? rom_2_data : 8'bz;  // Controlled_Buffer controlled_buffer_2
  Register_part #(.width(4)) register_4 (
    .D(controlled_buffer_1_out_2), .Q(register_4_q), .clk(not_5_out), .clr(Reset));  // open: en
  Counter #(.width(4), .max('hf)) counter_1 (
    .Q(counter_1_q), .clk(and_1_out), .clr(or_1_out));  // open: load, D, count, carry
  or or_1 (or_1_out, Reset, and_5_out, decoder_3_out3);
  assign controlled_buffer_3_out = or_9_out ? {controlled_buffer_1_out, controlled_buffer_1_out_2} : 8'bz;  // Controlled_Buffer controlled_buffer_3
  Decoder #(.select(4)) decoder_2 (
    .out0(decoder_2_out0), .out1(decoder_2_out1), .out2(decoder_2_out2), .out3(decoder_2_out3),
    .out4(decoder_2_out4), .sel(register_4_q));  // open: out5, out6, out7, out8, out9, out10, out11, out12, out13, out14, out15, en
  Decoder #(.select(4)) decoder_3 (
    .out0(decoder_3_out0), .out1(decoder_3_out1), .out2(decoder_3_out2), .out3(decoder_3_out3),
    .sel(counter_1_q));  // open: out4, out5, out6, out7, out8, out9, out10, out11, out12, out13, out14, out15, en
  Decoder #(.select(4)) decoder_4 (
    .out0(decoder_4_out0), .out1(decoder_4_out1), .out2(decoder_4_out2), .out3(decoder_4_out3),
    .out4(decoder_4_out4), .sel(register_5_q));  // open: out5, out6, out7, out8, out9, out10, out11, out12, out13, out14, out15, en
  Register_part #(.width(4)) register_5 (
    .D(controlled_buffer_1_out_2), .Q(register_5_q), .clk(not_4_out), .clr(Reset));  // open: en
  Register_part register_6 (.D(controlled_buffer_3_out), .Q(register_6_q), .clk(and_6_out), .clr(Reset));  // open: en
  and and_6 (and_6_out, decoder_2_out0, or_7_out);
  Register_part register_7 (.D(controlled_buffer_3_out), .Q(register_7_q), .clk(and_7_out), .clr(Reset));  // open: en
  and and_7 (and_7_out, decoder_2_out1, or_7_out);
  Register_part register_8 (.D(controlled_buffer_3_out), .Q(register_8_q), .clk(and_8_out), .clr(Reset));  // open: en
  and and_8 (and_8_out, decoder_2_out2, or_7_out);
  Register_part register_9 (
    .D(controlled_buffer_3_out), .Q({register_9_q_2, register_9_q, register_9_q_3}), .clk(or_2_out),
    .clr(Reset));  // open: en
  or or_2 (or_2_out, and_9_out, and_31_out);
  and and_9 (and_9_out, decoder_2_out3, or_7_out);
  Register_part register_10 (
    .D(controlled_buffer_3_out), .Q(register_10_q), .clk(and_10_out), .clr(Reset));  // open: en
  and and_10 (and_10_out, decoder_2_out4, or_7_out);
  Register_part #(.width(4)) register_11 (
    .D(controlled_buffer_1_out_2), .Q(register_11_q), .clk(not_3_out), .clr(Reset));  // open: en
  not not_3 (not_3_out, decoder_3_out0);
  assign controlled_buffer_3_out = and_11_out ? register_6_q : 8'bz;  // Controlled_Buffer controlled_buffer_4
  and and_11 (and_11_out, or_3_out, decoder_4_out0);
  assign controlled_buffer_3_out = and_12_out ? register_7_q : 8'bz;  // Controlled_Buffer controlled_buffer_5
  and and_12 (and_12_out, or_3_out, decoder_4_out1);
  assign controlled_buffer_3_out = and_13_out ? register_8_q : 8'bz;  // Controlled_Buffer controlled_buffer_6
  and and_13 (and_13_out, or_3_out, decoder_4_out2);
  assign controlled_buffer_3_out = and_14_out ? {register_9_q_2, register_9_q, register_9_q_3} : 8'bz;  // Controlled_Buffer controlled_buffer_7
  and and_14 (and_14_out, or_3_out, decoder_4_out3);
  assign controlled_buffer_3_out = and_15_out ? register_10_q : 8'bz;  // Controlled_Buffer controlled_buffer_8
  and and_15 (and_15_out, or_3_out, decoder_4_out4);
  not not_4 (not_4_out, and_16_out);
  or or_3 (or_3_out, and_39_out, and_18_out);
  or or_4 (or_4_out, and_22_out, and_50_out, and_35_out, and_37_out, and_29_out);
  and and_16 (and_16_out, or_4_out, and_1_out);
  not not_5 (not_5_out, and_17_out);
  and and_17 (and_17_out, and_1_out, or_5_out);
  or or_5 (or_5_out, and_23_out, and_26_out, and_34_out, and_39_out);
  or or_6 (or_6_out, and_24_out, and_51_out, and_36_out, and_50_out, and_30_out);
  and and_18 (and_18_out, or_6_out, and_1_out);
  and and_19 (and_19_out, and_1_out, or_8_out);
  or or_7 (or_7_out, and_39_out, and_19_out);
  or or_8 (or_8_out, and_20_out, and_25_out, and_33_out);
  buf or_9 (or_9_out, and_20_out);  // OR_Gate
  Comparator comparator_1 (
    .a(register_7_q), .b(register_8_q), .gt(comparator_1_gt), .eq(comparator_1_eq), .lt(comparator_1_lt));
  Multiplexer #(.select(2)) multiplexer_1 (
    .in0(comparator_1_gt), .in1(comparator_1_eq), .in2(comparator_1_lt), .out(multiplexer_1_out),
    .sel(register_9_q_3));  // open: in3, en
  Decoder #(.select(4)) decoder_5 (
    .out1(decoder_5_out1), .out2(decoder_5_out2), .out3(decoder_5_out3), .out4(decoder_5_out4),
    .out5(decoder_5_out5), .out6(decoder_5_out6), .out7(decoder_5_out7), .out8(decoder_5_out8),
    .out9(decoder_5_out9), .out10(decoder_5_out10), .out11(decoder_5_out11), .out13(decoder_5_out13),
    .out14(decoder_5_out14), .out15(decoder_5_out15), .sel(register_11_q));  // open: out0, out12, en
  and and_20 (and_20_out, decoder_3_out2, decoder_5_out14);
  not not_6 (not_6_out, and_27_out);
  assign controlled_buffer_9_out = and_36_out ? controlled_buffer_3_out : 8'bz;  // Controlled_Buffer controlled_buffer_9
  assign controlled_buffer_3_out = and_31_out ? alu_8bit_1_c0 : 8'bz;  // Controlled_Buffer controlled_buffer_10
  Register_part #(.width(1)) register_12 (
    .D(multiplexer_1_out), .Q(register_12_q), .clk(and_21_out), .clr(undriven));  // open: en
  and and_21 (and_21_out, not_9_out, decoder_5_out11);
  and and_22 (and_22_out, decoder_3_out1, decoder_5_out1);
  and and_23 (and_23_out, decoder_3_out1, decoder_5_out14);
  and and_24 (and_24_out, decoder_3_out2, decoder_5_out1);
  RAM #(.bus("separate")) ram_1 (
    .addr(register_10_q), .din(controlled_buffer_3_out), .data(ram_1_data), .clk(not_6_out), .clr(Reset));  // open: str, sel, ld
  ALU_8bit alu_8bit_1 (
    .A0(register_7_q[0]), .A1(register_7_q[1]), .A2(register_7_q[2]), .A3(register_7_q[3]),
    .A4(register_7_q[4]), .A5(register_7_q[5]), .A6(register_7_q[6]), .A7(register_7_q[7]),
    .B0(register_8_q[0]), .B1(register_8_q[1]), .B2(register_8_q[2]), .B3(register_8_q[3]),
    .B4(register_8_q[4]), .B5(register_8_q[5]), .B6(register_8_q[6]), .B7(register_8_q[7]),
    .O0(register_6_q[0]), .O1(register_6_q[1]), .O2(register_6_q[2]), .O3(register_6_q[3]),
    .C0(alu_8bit_1_c0[0]), .C1(alu_8bit_1_c0[1]), .C2(alu_8bit_1_c0[2]), .C3(alu_8bit_1_c0[3]),
    .C4(alu_8bit_1_c0[4]), .C5(alu_8bit_1_c0[5]), .C6(alu_8bit_1_c0[6]), .C7(alu_8bit_1_c0[7]));
  assign controlled_buffer_3_out = and_33_out ? {1'b0, keyboard_1_data} : 8'bz;  // Controlled_Buffer controlled_buffer_11
  and and_25 (and_25_out, decoder_3_out2, decoder_5_out2);
  and and_26 (and_26_out, decoder_3_out1, decoder_5_out2);
  buf or_10 (or_10_out, and_24_out);  // OR_Gate
  and and_27 (and_27_out, and_1_out, or_10_out);
  TTY #(.rows(15)) tty_1 (.data(controlled_buffer_9_out[6:0]), .clk(and_40_out), .clr(Reset));  // open: we
  or or_11 (or_11_out, decoder_5_out15, and_28_out);
  and and_28 (and_28_out, and_34_out, not_7_out);
  not not_7 (not_7_out, keyboard_1_avail);
  and and_29 (and_29_out, decoder_3_out1, register_12_q, decoder_5_out3);
  and and_30 (and_30_out, decoder_3_out2, register_12_q, decoder_5_out3);
  and and_31 (and_31_out, decoder_3_out2, decoder_5_out4);
  buf or_12 (or_12_out, and_25_out);  // OR_Gate
  assign controlled_buffer_3_out = or_12_out ? ram_1_data : 8'bz;  // Controlled_Buffer controlled_buffer_12
  Keyboard keyboard_1 (.clk(not_8_out), .clr(Reset), .avail(keyboard_1_avail), .data(keyboard_1_data));  // open: re
  // AND_Gate and_32 has open pins: in0=decoder_3_out1, in1=decoder_5_out4, out=open
  and and_33 (and_33_out, decoder_3_out2, decoder_5_out5);
  and and_34 (and_34_out, decoder_3_out1, decoder_5_out5);
  not not_8 (not_8_out, and_33_out);
  and and_35 (and_35_out, decoder_3_out1, decoder_5_out6);
  and and_36 (and_36_out, decoder_3_out2, decoder_5_out6);
  not not_9 (not_9_out, and_1_out);
  and and_37 (and_37_out, decoder_3_out1, decoder_5_out7);
  // AND_Gate and_38 has open pins: in0=decoder_3_out2, in1=decoder_5_out8, out=open
  and and_39 (and_39_out, decoder_3_out2, decoder_5_out7);
  and and_40 (and_40_out, and_36_out, not_9_out);
  // AND_Gate and_41 has open pins: in0=decoder_3_out1, in1=decoder_5_out9, out=open
  // AND_Gate and_42 has open pins: in0=decoder_3_out1, in1=decoder_5_out8, out=open
  // AND_Gate and_43 has open pins: in0=decoder_3_out2, in1=decoder_5_out9, out=open
  // AND_Gate and_44 has open pins: in0=decoder_3_out1, in1=decoder_5_out10, out=open
  // AND_Gate and_45 has open pins: in0=decoder_3_out2, in1=decoder_5_out10, out=open
  // AND_Gate and_46 is placed but not wired
  // AND_Gate and_47 is placed but not wired
  // AND_Gate and_48 is placed but not wired
  // AND_Gate and_49 is placed but not wired
  and and_50 (and_50_out, decoder_5_out13, decoder_3_out1);
  and and_51 (and_51_out, decoder_5_out13, decoder_3_out2);

  // Notes on the sheet:
  //   BIOS
  //   HDD1
  //   contents of rom_1 (hex, n*v repeats v):
  //   e 1 10 e 3 1 3 1 0 6 0 0 e 0 72 6 0 0 e 0 6f 6 0 0 e 0 77 6 0 0 e 0 61 6 0 0 e 0 64 6 0 0 e 0 7a 6 0
  //   0 e 0 69 6 0 0 5 1 0 e 2 31 e 3 1 b 0 0 e 0 54 3 0 0 e 0 d 6 0 0 e 0 41 6 0 0 f
  //   contents of rom_2 (hex, n*v repeats v):
  //   e 0 0 d 0 0 e 0 70 6 0 0 e 0 72 6 0 0 e 0 6f 6 0 0 e 0 77 6 0 0 e 0 61 6 0 0 e 0 64 6 0 0 e 0 7a 6 0
  //   0 e 0 69 6 0 0 5 1 0 e 2 31 e 3 1 b 0 0 e 0 54 3 0 0 e 0 d 6 0 0 e 0 41 6 0 0 f
  //   GET
  //   R0
  //   R1
  //   R2
  //   R3
  //   R4
  //   PUT
  //   ALU
  //   Compare
  //   RAM
  //   Decoder
  //   Keyboard
  //   Terminal
endmodule

module ALU_8bit (
  input  O0,
  input  O1,
  input  A0,
  input  O2,
  input  A1,
  input  O3,
  input  A2,
  input  A3,
  input  A4,
  input  A5,
  input  A6,
  input  A7,
  input  B0,
  input  B1,
  input  B2,
  input  B3,
  input  B4,
  input  B5,
  input  B6,
  input  B7,
  output C0,
  output C1,
  output C2,
  output C3,
  output C4,
  output C5,
  output C6,
  output C7
);

  wire [7:0] adder_1_out, and_1_out, divider_1_out, multiplier_1_out, nand_1_out, nor_1_out, not_1_out,
       or_1_out, subtractor_1_out, xor_1_out;

  assign and_1_out = {A7, A6, A5, A4, A3, A2, A1, A0} & {B7, B6, B5, B4, B3, B2, B1, B0};  // AND_Gate and_1, 8 bits wide
  assign or_1_out = {A7, A6, A5, A4, A3, A2, A1, A0} | {B7, B6, B5, B4, B3, B2, B1, B0};  // OR_Gate or_1, 8 bits wide
  assign xor_1_out = {A7, A6, A5, A4, A3, A2, A1, A0} ^ {B7, B6, B5, B4, B3, B2, B1, B0};  // XOR_Gate xor_1, 8 bits wide
  assign nand_1_out = ~({A7, A6, A5, A4, A3, A2, A1, A0} & {B7, B6, B5, B4, B3, B2, B1, B0});  // NAND_Gate nand_1, 8 bits wide
  assign nor_1_out = ~({A7, A6, A5, A4, A3, A2, A1, A0} | {B7, B6, B5, B4, B3, B2, B1, B0});  // NOR_Gate nor_1, 8 bits wide
  Adder adder_1 (
    .a({A7, A6, A5, A4, A3, A2, A1, A0}), .b({B7, B6, B5, B4, B3, B2, B1, B0}), .out(adder_1_out));  // open: cin, cout
  Subtractor subtractor_1 (
    .a({A7, A6, A5, A4, A3, A2, A1, A0}), .b({B7, B6, B5, B4, B3, B2, B1, B0}), .out(subtractor_1_out));  // open: bin, bout
  Multiplier multiplier_1 (
    .a({A7, A6, A5, A4, A3, A2, A1, A0}), .b({B7, B6, B5, B4, B3, B2, B1, B0}), .out(multiplier_1_out));  // open: cin, cout
  Divider divider_1 (
    .a({A7, A6, A5, A4, A3, A2, A1, A0}), .b({B7, B6, B5, B4, B3, B2, B1, B0}), .out(divider_1_out));  // open: upper, rem
  assign not_1_out = ~{A7, A6, A5, A4, A3, A2, A1, A0};  // NOT_Gate not_1, 8 bits wide
  Multiplexer #(.select(4), .width(8)) multiplexer_1 (
    .in0({A7, A6, A5, A4, A3, A2, A1, A0}), .in1(not_1_out), .in2(and_1_out), .in3(or_1_out),
    .in4(xor_1_out), .in5(nand_1_out), .in6(nor_1_out), .in7({8{1'b1}}), .in8({8{1'b0}}), .in9(adder_1_out),
    .in10(subtractor_1_out), .in11(multiplier_1_out), .in12(divider_1_out),
    .out({C7, C6, C5, C4, C3, C2, C1, C0}), .sel({O3, O2, O1, O0}));  // open: in13, in14, in15, en
endmodule

module Register (
  input  [7:0] In,
  input  S,
  input  C,
  input  R,
  output [7:0] Out
);

  wire and_1_out, not_1_out, or_1_out;

  or or_1 (or_1_out, S, and_1_out);
  and and_1 (and_1_out, not_1_out, C);
  not not_1 (not_1_out, S);
  Counter counter_1 (.load(S), .D(In), .count(and_1_out), .Q(Out), .clk(or_1_out), .clr(R));  // open: carry
endmodule
